# Fritzing sketch RTTY-ARDUINO (saved by Fritzing 0.9.0b)

parts:
  Componente1 = Arduino Nano (Rev3.0) (ICSP)
  U1 = 2.5mm Audio Jack [package=stereojack2.5mm_smd]
  LED1 = LED - 5mm [color="Red (633nm)" package="5 mm [THT]"]  # not connected
  SG1 = Buzzer 12mm [package=buzzer-ccv-kit]  # not connected
  R1 = Resistor [tolerance=±5% resistance=220 package=THT]
  R3 = Resistor [tolerance=±5% resistance=10k package="0603 [SMD]"]
  LED2 = LED - 5mm [color="Green (560nm)" package="5 mm [THT]"]
  R4 = Resistor [tolerance=±5% resistance=220 package=THT]

nets:
  N1: Componente1.D4, R3.Pin_1
  N2: Componente1.D12/MISO, R1.Pin_1
  N3: Componente1.GND, U1.SLEEVE, LED2.cathode
  N4: Componente1.D13/SCK, R4.Pin_1
  N5: U1.RIGHT, R3.Pin_0

notes:
  10K
  220
  BUZZER
  +
  -
  AZUL - NA CABECA DO P2
  PRETO - GND DO P2 ULTIMA PARTE
  VERMELHO - PARTE CENTRAL DO P2
  ESQUEMA DE CONEXAO DO P2 PARA O RADIO BAOFENG UV5R E DERIVADOS
  TTL DE ENVIO ATIVADO
  PTT ATIVADO
  ACESO AO TRANSMITIR
  PISCANTE AO TRANSMITIR
